# Fritzing sketch ESP8266-bmp180 (saved by Fritzing 0.9.10b)
breadboards: 1

parts:
  U2 = ESP8266 WiFi Module [part_number=ESP8266]
  Componente1 = Barometric Pressure Sensor - BMP180 Breakout (GY-68)

nets:
  VCC: U2.VCC, Componente1.VCC
  N1: U2.GPIO_0, Componente1.SDA
  N2: U2.GPIO_2, Componente1.SCL
  GND: U2.GND, Componente1.GND

custom parts:
  ESP8266 WiFi Module: Generic WiFi Module based on the ESP8266 with onboard PCB antenna and UART communications
