# Fritzing sketch Water-Rocket (saved by Fritzing 0.9.10b)
circuit board: 6.80129cm x 5.15947cm
breadboards: 1

parts:
  GY-91_(MPU-6050) = MPU-6050 Board GY-521 [form="♀ (female)" package=THT]
  C1 = Electrolytic Capacitor [capacitance=1μF voltage=35V package="0405 [SMD, electrolytic]"]
  MCU1 = Banana Pi Zero
  S1 = Pushbutton [package="[THT]"]
  R1 = Resistor [tolerance=±5% power=0.25 resistance=4700 package=THT]
  R2 = Resistor [tolerance=±5% power=0.25 resistance=56 package=THT]
  R3 = Resistor [tolerance=±5% power=0.25 resistance=56 package=THT]
  U1 = LIPO-1000mAh [package=lipo-1000]
  J1 = Basic Servo
  LED3 = LED - 5mm [color="Orange (620nm)" current=0.030 package="5 mm [THT]"]
  LED4 = LED - 5mm [color="White (4500K)" current=0.030 package="5 mm [THT]"]

nets:
  N1: GY-91_(MPU-6050).pin1, C1.+, MCU1.pin_2, MCU1.pin_4, R1.Pin_1, U1.+, J1.vcc
  N2: GY-91_(MPU-6050).pin2, C1.-, MCU1.pin_6, MCU1.pin_8, MCU1.pin_20, MCU1.pin_34, S1.Pin_1, S1.Pin_2, U1.-, J1.gnd, LED3.cathode, LED4.cathode
  N3: GY-91_(MPU-6050).pin3, MCU1.pin_5
  N4: GY-91_(MPU-6050).pin4, MCU1.pin_3
  N5: MCU1.pin_12, S1.Pin_3, S1.Pin_4, R1.Pin_0
  N6: MCU1.pin_16, R2.Pin_0
  N7: MCU1.pin_18, R3.Pin_0
  N8: MCU1.pin_33, J1.pulse
  N9: R2.Pin_1, LED3.anode
  N10: R3.Pin_1, LED4.anode

notes:
  Lithium battery uses MT3608 StepUp to reach 5V

custom parts:
  MPU-6050 Board GY-521: Acelerometro y Giroscopio MPU-6050 Board GY-521
  Banana Pi Zero: The Banana Pi Zero is half the size of a Model A+, with twice the utility. A tiny Raspberry Pi that’s affordable enough for any project! · 1Ghz, Single-core CPU · 512MB RAM · Mini HDMI and USB On-The-Go ports · Micro USB power · HAT-compatible 40-pin header. Jan 2018: In this version schematic has been changed so the pins match the GPIO connector. I.e. the left hand pins are all the pins (the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
